# Fritzing sketch FIRE ALARM (saved by Fritzing 0.8.7b)
breadboards: 1

parts:
  DHT1 = DHT11 Humitidy and Temperature Sensor
  Mod1 = KY-026 Flame Sensor Module [package="Breakout board"]
  U1 = NodeMCU V1.0

nets:
  VDD: DHT1.VDD, Mod1.+, U1.3V3
  N1: DHT1.DATA, U1.D3
  GND: DHT1.GND, Mod1.G, U1.GND
  N2: Mod1.D0, U1.D2

custom parts:
  DHT11 Humitidy and Temperature Sensor: DHT11 Humidity and Temperature Sensor
  KY-026 Flame Sensor Module: KY-026 Flame Sensor Module reacts in the presence of fire.
  NodeMCU V1.0: ESP8266 based NodeMCU
